# Fritzing sketch schematic (saved by Fritzing 0.9.3b)
breadboards: 1

parts:
  U1 = ESP32-38PinWide [part_number=ESP32-38PinWide]
  C1 = Capacitor Polarized [package=cpol-radial-100uf-25v]
  SIM800L_BO1 = SIM800L BO
  U2 = LIPO-110mAh [package=lipo-110]

nets:
  N1: U1.EN, C1.+
  N2: U1.GPIO26, SIM800L_BO1.pin_5
  N3: U1.GPIO27, SIM800L_BO1.pin_4
  N4: U1.GPIO11, C1.-, SIM800L_BO1.pin_6, U2.-
  N5: SIM800L_BO1.PIN2, U2.+

custom parts:
  ESP32-38PinWide: Generic 38-Pin ESP32 with wide format (only access to one side of pins on a breadboard) based on Stephen Lilley's HiLetgo ESP-WROOM-32 ESP32 ESP-32S Development Board.
